# Fritzing sketch wiring (saved by Fritzing 0.9.3b)
breadboards: 2

parts:
  Raspberry_Pi_Zero1 = Raspberry Pi Zero
  S1_-_PTT_Switch = Pushbutton [package="[THT]"]
  R1 = Resistor [tolerance=±5% resistance=330 package="2010 [SMD]"]
  LED1_-_PTT_Indicator = LED - 3mm [color="Red (633nm)" package="3 mm [THT]"]
  R2 = Resistor [tolerance=±5% resistance=330 package="2010 [SMD]"]
  LED2_-_Participant_Ind = LED - 3mm [color="Red (633nm)" package="3 mm [THT]"]
  R3 = Resistor [tolerance=±5% resistance=330 package="2010 [SMD]"]
  LED3_-_Online_Ind = LED - 3mm [color="Red (633nm)" package="3 mm [THT]"]
  S2_-_Wifi_Reset = Pushbutton [package="[THT]"]
  S3_-_Volume_Up = Pushbutton [package="[THT]"]
  S4_-_Volume_Down = Pushbutton [package="[THT]"]
  J1 = female pin header, 2 pins [form="♀ (female)"]

nets:
  N1: Raspberry_Pi_Zero1.GPIO17, S2_-_Wifi_Reset.Pin_3, S2_-_Wifi_Reset.Pin_4
  N2: Raspberry_Pi_Zero1.GPIO27, S3_-_Volume_Up.Pin_3, S3_-_Volume_Up.Pin_4
  N3: Raspberry_Pi_Zero1.GPIO22, S4_-_Volume_Down.Pin_3, S4_-_Volume_Down.Pin_4
  N4: Raspberry_Pi_Zero1.GND, S1_-_PTT_Switch.Pin_1, S1_-_PTT_Switch.Pin_2, R1.Pin_1, R2.Pin_1, R3.Pin_1, S2_-_Wifi_Reset.Pin_1, S2_-_Wifi_Reset.Pin_2, S3_-_Volume_Up.Pin_1, S3_-_Volume_Up.Pin_2, S4_-_Volume_Down.Pin_1, S4_-_Volume_Down.Pin_2, J1.pin1
  N5: Raspberry_Pi_Zero1.GPIO25, S1_-_PTT_Switch.Pin_3, S1_-_PTT_Switch.Pin_4
  N6: Raspberry_Pi_Zero1.GPIO24, LED1_-_PTT_Indicator.anode
  N7: Raspberry_Pi_Zero1.GPIO23, LED2_-_Participant_Ind.anode
  N8: Raspberry_Pi_Zero1.GPIO18, LED3_-_Online_Ind.anode
  N9: Raspberry_Pi_Zero1.5V, J1.pin2
  N10: R1.Pin_0, LED1_-_PTT_Indicator.cathode
  N11: R2.Pin_0, LED2_-_Participant_Ind.cathode
  N12: R3.Pin_0, LED3_-_Online_Ind.cathode
